# Fritzing sketch ATTinySecretKnock (saved by Fritzing 0.7.4b)
breadboards: 1

parts:
  J1 = Piezo Speaker
  R4 = Resistor [resistance=1M tolerance=±5% package=THT]
  Arduino1 = Arduino

nets:
  N1: J1.pin1, R4.Pin_0, Arduino1.GND
  N2: J1.pin2, R4.Pin_1, Arduino1.A0

notes:
  A Piezo is an electronic device that can both be used to play tones and to detect tones. In this project, a Piezo captures a knock and sends a string "Knock!" back to the computer over the serial port. In order to see this text you can use the Arduino serial monitor.
  http://arduino.cc/en/Tutorial/Knock
