# Fritzing sketch ATTinyServo (saved by Fritzing 0.7.4b)

parts:
  U1 = attiny85 [package=dip]
  J1 = male pin header, 3 pins [form="♂ (male)"]
  J2 = male pin header, 3 pins [form="♂ (male)"]
  J3 = male pin header, 3 pins [form="♂ (male)"]
  J4 = male pin header, 3 pins [form="♂ (male)"]
  J5 = male pin header, 3 pins [form="♂ (male)"]
  S1 = Pushbutton [package="[THT]"]
  R1 = Resistor [tolerance=±5% resistance=10k package=THT]
  J6 = male pin header, 2 pins [form="♂ (male)"]
  J7 = Screw terminal - 2 pins [package=THT]
  Y1 = Resonator [frequency="16 Mhz" package=THT]
  J8 = Screw terminal - 2 pins [package=THT]

nets:
  N1: U1.Pin_1, R1.Pin_1
  N2: U1.Pin_2, J4.pin1, Y1.0
  N3: U1.Pin_3, J5.pin1, Y1.pin_1
  GND: U1.Pin_4, J1.pin3, J2.pin3, J3.pin3, J4.pin3, J5.pin3, S1.Pin_3, S1.Pin_4, J6.pin2, J7.pin2, Y1.GND, J8.pin2
  N4: U1.Pin_5, J3.pin1
  N5: U1.Pin_6, J2.pin1
  N6: U1.Pin_7, J1.pin1
  5V: U1.Pin_8, S1.Pin_1, S1.Pin_2, R1.Pin_0, J6.pin1, J7.pin1
  12V: J1.pin2, J2.pin2, J3.pin2, J4.pin2, J5.pin2, J8.pin1
