# Fritzing sketch ArduinoISPBareBones3Chips (saved by Fritzing 0.7.4b)
breadboards: 1

parts:
  Arduino1 = Arduino
  C1 = Electrolytic Capacitor [capacitance=10µF voltage=35V package="100 mil [THT, electrolytic]"]
  U1 = attiny85 [package=dip]

nets:
  GND: Arduino1.GND, C1.-, U1.Pin_4
  N1: Arduino1.D13, U1.Pin_7
  N2: Arduino1.D12, U1.Pin_6
  N3: Arduino1.D11, U1.Pin_5
  N4: Arduino1.D10, U1.Pin_1
  N5: Arduino1.RST, C1.+
  5V: Arduino1.+5V, U1.Pin_8
